# Fritzing sketch 2016SummerCraft (saved by Fritzing 0.9.3b)
circuit board: 16.0044cm x 9.65972cm
perfboards: 1
stripboards: 4

parts:
  Raspberry_Pi2 = Raspberry Pi (Model B)
  U2 = LCD-16X2 [package=lcd-8x2]
  R19 = Trimmer Potentiometer [maximum_resistance=10kΩ package=THT]
  R20 = Resistor [tolerance=±5% resistance=220 package=THT]
  R21 = Resistor [tolerance=±5% resistance=220 package=THT]
  R22 = Resistor [tolerance=±5% resistance=220 package=THT]
  R23 = Resistor [tolerance=±5% resistance=220 package=THT]
  R24 = Resistor [tolerance=±5% resistance=220 package=THT]
  S11 = Round Pushbutton  # not connected
  S12 = Round Pushbutton  # not connected
  S13 = Round Pushbutton  # not connected
  S14 = Round Pushbutton  # not connected
  S15 = Round Pushbutton  # not connected
  LED9 = LED - 5mm [color="Red (633nm)" package="5 mm [THT]"]
  R25 = Resistor [tolerance=±5% resistance=220 package=THT]
  LED10 = LED - 5mm [color="Red (633nm)" package="5 mm [THT]"]
  R26 = Resistor [tolerance=±5% resistance=220 package=THT]
  LED11 = LED - 5mm [color="Red (633nm)" package="5 mm [THT]"]
  R27 = Resistor [tolerance=±5% resistance=220 package=THT]
  LED12 = LED - 5mm [color="Red (633nm)" package="5 mm [THT]"]
  R28 = Resistor [tolerance=±5% resistance=220 package=THT]

nets:
  N1: Raspberry_Pi2.SDA, LED9.anode, R25.Pin_0, R25.Pin_1
  N2: Raspberry_Pi2.SCL, LED10.anode, R26.Pin_0, R26.Pin_1
  N3: Raspberry_Pi2.#4, LED11.anode, R27.Pin_0, R27.Pin_1
  N4: Raspberry_Pi2.TXD, U2.DB6
  N5: Raspberry_Pi2.RXD, U2.A
  N6: Raspberry_Pi2.#17, LED12.anode, R28.Pin_0, R28.Pin_1
  N7: Raspberry_Pi2.#18, U2.K
  N8: Raspberry_Pi2.#21, R20.Pin_0
  N9: Raspberry_Pi2.#22, R21.Pin_0
  N10: Raspberry_Pi2.MOSI, R22.Pin_0
  N11: Raspberry_Pi2.MISO, R23.Pin_0
  N12: Raspberry_Pi2.#25, U2.RS
  N13: Raspberry_Pi2.SCLK, R24.Pin_0
  N14: U2.VDD, R21.Pin_1
  N15: U2.VO, R19.wiper
  N16: U2.R_W, R20.Pin_1

custom parts:
  Raspberry Pi (Model B): Raspberry Pi Single-board Computer, Model B
